// Logisim project Circuito_SRC_2.circ as structural Verilog: 14 circuits, main circuit main
module main (
  input  [3:0] A,
  input  [3:0] B,
  input  num_res,
  input  sum_res,
  input  ncomp
);

  wire [3:0] restador_bcd_1_borrow, restador_bcd_1_salida, sumador_bcd_1_out_3, sumador_bcd_1_out_4;
  wire [6:0] comparador_1_salida_a_dec, dec_7_seg_1_g, dec_7_seg_2_g, multiplexer_3_out, multiplexer_4_out;
  wire [7:0] multiplexer_1_out, multiplexer_2_out;

  Sumador_BCD sumador_bcd_1 (.A(A), .B(B), .out_3(sumador_bcd_1_out_3), .out_4(sumador_bcd_1_out_4));
  Restador_BCD restador_bcd_1 (.A(A), .B(B), .Salida(restador_bcd_1_salida), .Borrow(restador_bcd_1_borrow));
  Comparador comparador_1 (.A(A), .B(B), .Salida_a_Dec(comparador_1_salida_a_dec));
  Multiplexer #(.width(8), .enable("false")) multiplexer_1 (
    .in0({sumador_bcd_1_out_4, sumador_bcd_1_out_3}), .in1({restador_bcd_1_borrow, restador_bcd_1_salida}),
    .out(multiplexer_1_out), .sel(sum_res));
  Multiplexer #(.width(8), .enable("false")) multiplexer_2 (
    .in0({B, A}), .in1(multiplexer_1_out), .out(multiplexer_2_out), .sel(num_res));
  Dec_7_seg dec_7_seg_1 (
    .in_1(multiplexer_2_out[7:4]), .a(dec_7_seg_1_g[6]), .b(dec_7_seg_1_g[5]), .c(dec_7_seg_1_g[4]),
    .d(dec_7_seg_1_g[3]), .e(dec_7_seg_1_g[2]), .f(dec_7_seg_1_g[1]), .g(dec_7_seg_1_g[0]));
  Dec_7_seg dec_7_seg_2 (
    .in_1(multiplexer_2_out[3:0]), .a(dec_7_seg_2_g[6]), .b(dec_7_seg_2_g[5]), .c(dec_7_seg_2_g[4]),
    .d(dec_7_seg_2_g[3]), .e(dec_7_seg_2_g[2]), .f(dec_7_seg_2_g[1]), .g(dec_7_seg_2_g[0]));
  Multiplexer #(.width(7), .enable("false")) multiplexer_3 (
    .in0(dec_7_seg_1_g), .out(multiplexer_3_out), .sel(ncomp));  // open: in1
  Multiplexer #(.width(7), .enable("false")) multiplexer_4 (
    .in0(dec_7_seg_2_g), .in1(comparador_1_salida_a_dec), .out(multiplexer_4_out), .sel(ncomp));
  _7_Segment_Display u_7_segment_display_1 (
    .g(multiplexer_4_out[0]), .f(multiplexer_4_out[1]), .a(multiplexer_4_out[6]), .b(multiplexer_4_out[5]),
    .e(multiplexer_4_out[2]), .d(multiplexer_4_out[3]), .c(multiplexer_4_out[4]));  // open: dp
  _7_Segment_Display u_7_segment_display_2 (
    .g(multiplexer_3_out[0]), .f(multiplexer_3_out[1]), .a(multiplexer_3_out[6]), .b(multiplexer_3_out[5]),
    .e(multiplexer_3_out[2]), .d(multiplexer_3_out[3]), .c(multiplexer_3_out[4]));  // open: dp
endmodule

module Sumador_BCD (
  input  [3:0] A,
  input  [3:0] B,
  output [3:0] out_3,
  output [3:0] out_4
);

  wire and_1_out, and_2_out, and_3_out, and_4_out;
  wire [2:2] or_1_out, or_2_out;
  wire [4:0] sumador_4_bits_1_s;
  wire [5:0] sumador_5_bits_1_s;

  Sumador_4_bits sumador_4_bits_1 (.A(A), .B(B), .S(sumador_4_bits_1_s[3:0]), .C1(sumador_4_bits_1_s[4]));
  Sumador_5_bits sumador_5_bits_1 (
    .A(sumador_4_bits_1_s), .B({2'b00, {2{or_1_out[2]}}, 1'b0}), .S(sumador_5_bits_1_s[4:0]),
    .C1(sumador_5_bits_1_s[5]));
  and and_1 (and_1_out, sumador_4_bits_1_s[2], sumador_4_bits_1_s[3]);
  and and_2 (and_2_out, sumador_4_bits_1_s[3], sumador_4_bits_1_s[1]);
  or or_1 (or_1_out[2], sumador_4_bits_1_s[4], and_1_out, and_2_out);
  Sumador_6_bits sumador_6_bits_1 (
    .A(sumador_5_bits_1_s), .B({3'b000, {2{or_2_out[2]}}, 1'b0}), .S({out_4[1:0], out_3}));  // open: C1
  and and_3 (and_3_out, sumador_5_bits_1_s[2], sumador_5_bits_1_s[3]);
  and and_4 (and_4_out, sumador_5_bits_1_s[3], sumador_5_bits_1_s[1]);
  or or_2 (or_2_out[2], sumador_5_bits_1_s[5], and_3_out, and_4_out);

  assign out_4[3:2] = 2'b00;
endmodule

module Sumador_4_bits (
  input  [3:0] A,
  input  [3:0] B,
  output [3:0] S,
  output C1
);

  wire and_1_out, and_2_out, and_3_out, and_4_out, and_5_out, and_6_out, and_7_out, or_1_out, or_2_out,
       xor_2_out, xor_3_out, xor_4_out, xor_5_out, xor_6_out, xor_7_out;

  xor xor_1 (S[0], A[0], B[0]);
  and and_1 (and_1_out, A[0], B[0]);
  xor xor_2 (xor_2_out, A[1], B[1]);
  xor xor_3 (xor_3_out, A[2], B[2]);
  and and_2 (and_2_out, A[1], B[1]);
  and and_3 (and_3_out, and_1_out, xor_2_out);
  xor xor_4 (xor_4_out, A[3], B[3]);
  xor xor_5 (xor_5_out, A[1], B[1]);
  xor xor_6 (xor_6_out, A[2], B[2]);
  and and_4 (and_4_out, A[2], B[2]);
  and and_5 (and_5_out, or_1_out, xor_3_out);
  xor xor_7 (xor_7_out, A[3], B[3]);
  and and_6 (and_6_out, A[3], B[3]);
  and and_7 (and_7_out, or_2_out, xor_4_out);
  xor xor_8 (S[1], xor_5_out, and_1_out);
  or or_1 (or_1_out, and_2_out, and_3_out);
  xor xor_9 (S[2], xor_6_out, or_1_out);
  or or_2 (or_2_out, and_4_out, and_5_out);
  xor xor_10 (S[3], xor_7_out, or_2_out);
  or or_3 (C1, and_6_out, and_7_out);
endmodule

module Restador_4_bits (
  input  [3:0] A,
  input  [3:0] B,
  output [3:0] S,
  output B1
);

  wire and_1_out, and_2_out, and_3_out, and_4_out, and_5_out, and_6_out, and_7_out, not_1_out, not_2_out,
       not_3_out, not_4_out, or_1_out, or_2_out, xor_1_out, xor_2_out, xor_3_out, xor_4_out, xor_5_out,
       xor_6_out;

  not not_1 (not_1_out, A[0]);
  not not_2 (not_2_out, A[1]);
  xor xor_1 (xor_1_out, B[1], and_7_out);
  not not_3 (not_3_out, A[2]);
  xor xor_2 (xor_2_out, B[2], or_1_out);
  not not_4 (not_4_out, A[3]);
  xor xor_3 (xor_3_out, B[3], or_2_out);
  xor xor_4 (xor_4_out, A[1], B[1]);
  and and_1 (and_1_out, not_2_out, xor_1_out);
  and and_2 (and_2_out, B[1], and_7_out);
  xor xor_5 (xor_5_out, A[2], B[2]);
  and and_3 (and_3_out, not_3_out, xor_2_out);
  and and_4 (and_4_out, B[2], or_1_out);
  xor xor_6 (xor_6_out, A[3], B[3]);
  and and_5 (and_5_out, not_4_out, xor_3_out);
  and and_6 (and_6_out, B[3], or_2_out);
  xor xor_7 (S[0], A[0], B[0]);
  and and_7 (and_7_out, not_1_out, B[0]);
  xor xor_8 (S[1], xor_4_out, and_7_out);
  or or_1 (or_1_out, and_1_out, and_2_out);
  xor xor_9 (S[2], xor_5_out, or_1_out);
  or or_2 (or_2_out, and_3_out, and_4_out);
  xor xor_10 (S[3], xor_6_out, or_2_out);
  or or_3 (B1, and_5_out, and_6_out);
endmodule

module Restador_BCD (
  input  [3:0] A,
  input  [3:0] B,
  output [3:0] Salida,
  output [3:0] Borrow
);

  wire menor_1_salida;
  wire [3:0] complemento_a_2_1_salida, complemento_a_2_2_salida, demultiplexer_1_out0, demultiplexer_1_out1,
       demultiplexer_2_out0, demultiplexer_2_out1, not_1_out, sumador_4_bits_1_s, sumador_4_bits_2_s,
       sumador_4_bits_3_s;

  Menor menor_1 (.A(A), .B(B), .Salida(menor_1_salida));
  Demultiplexer #(.width(4), .enable("false")) demultiplexer_1 (
    .out0(demultiplexer_1_out0), .out1(demultiplexer_1_out1), .in(A), .sel(menor_1_salida));
  Demultiplexer #(.width(4), .enable("false")) demultiplexer_2 (
    .out0(demultiplexer_2_out0), .out1(demultiplexer_2_out1), .in(B), .sel(menor_1_salida));
  Complemento_a_2 complemento_a_2_1 (.Entrada(demultiplexer_2_out1), .Salida(complemento_a_2_1_salida));
  Complemento_a_2 complemento_a_2_2 (.Entrada(demultiplexer_2_out0), .Salida(complemento_a_2_2_salida));
  Sumador_4_bits sumador_4_bits_1 (
    .A(demultiplexer_1_out1), .B(complemento_a_2_1_salida), .S(sumador_4_bits_1_s));  // open: C1
  Sumador_4_bits sumador_4_bits_2 (
    .A(demultiplexer_1_out0), .B(complemento_a_2_2_salida), .S(sumador_4_bits_2_s));  // open: C1
  assign not_1_out = ~sumador_4_bits_1_s;  // NOT_Gate not_1, 4 bits wide
  Sumador_4_bits sumador_4_bits_3 (.A(not_1_out), .B(4'b0001), .S(sumador_4_bits_3_s));  // open: C1
  Multiplexer #(.width(8), .enable("false")) multiplexer_1 (
    .in0({4'b0000, sumador_4_bits_2_s}), .in1({4'b0001, sumador_4_bits_3_s}), .out({Borrow, Salida}),
    .sel(menor_1_salida));
endmodule

module Igualador (
  input  [3:0] A,
  input  [3:0] B,
  output Igualdad
);

  wire xnor_1_out, xnor_2_out, xnor_3_out, xnor_4_out;

  xnor xnor_1 (xnor_1_out, A[0], B[0]);
  xnor xnor_2 (xnor_2_out, A[1], B[1]);
  xnor xnor_3 (xnor_3_out, A[2], B[2]);
  xnor xnor_4 (xnor_4_out, A[3], B[3]);
  and and_1 (Igualdad, xnor_1_out, xnor_2_out, xnor_3_out, xnor_4_out);
endmodule

module Mayor (
  input  [3:0] A,
  input  [3:0] B,
  output Salida
);

  wire and_1_out, and_2_out, and_3_out, and_4_out, not_1_out, not_2_out, not_3_out, not_4_out, xnor_1_out,
       xnor_2_out, xnor_3_out, xnor_4_out, xnor_5_out, xnor_6_out;

  xnor xnor_1 (xnor_1_out, A[3], B[3]);
  xnor xnor_2 (xnor_2_out, A[2], B[2]);
  xnor xnor_3 (xnor_3_out, A[1], B[1]);
  not not_1 (not_1_out, B[0]);
  and and_1 (and_1_out, A[0], not_1_out, xnor_1_out, xnor_2_out, xnor_3_out);
  not not_2 (not_2_out, B[1]);
  xnor xnor_4 (xnor_4_out, A[2], B[2]);
  xnor xnor_5 (xnor_5_out, A[3], B[3]);
  xnor xnor_6 (xnor_6_out, A[3], B[3]);
  and and_2 (and_2_out, A[1], not_2_out, xnor_4_out, xnor_5_out);
  not not_3 (not_3_out, B[2]);
  and and_3 (and_3_out, A[2], not_3_out, xnor_6_out);
  not not_4 (not_4_out, B[3]);
  and and_4 (and_4_out, A[3], not_4_out);
  or or_1 (Salida, and_1_out, and_2_out, and_3_out, and_4_out);
endmodule

module Menor (
  input  [3:0] A,
  input  [3:0] B,
  output Salida
);

  wire and_1_out, and_2_out, and_3_out, and_4_out, not_1_out, not_2_out, not_3_out, not_4_out, xnor_1_out,
       xnor_2_out, xnor_3_out, xnor_4_out, xnor_5_out, xnor_6_out;

  xnor xnor_1 (xnor_1_out, A[3], B[3]);
  xnor xnor_2 (xnor_2_out, A[2], B[2]);
  xnor xnor_3 (xnor_3_out, A[1], B[1]);
  not not_1 (not_1_out, A[0]);
  and and_1 (and_1_out, not_1_out, B[0], xnor_1_out, xnor_2_out, xnor_3_out);
  not not_2 (not_2_out, A[1]);
  xnor xnor_4 (xnor_4_out, A[2], B[2]);
  xnor xnor_5 (xnor_5_out, A[3], B[3]);
  xnor xnor_6 (xnor_6_out, A[3], B[3]);
  and and_2 (and_2_out, not_2_out, B[1], xnor_4_out, xnor_5_out);
  not not_3 (not_3_out, A[2]);
  and and_3 (and_3_out, not_3_out, B[2], xnor_6_out);
  not not_4 (not_4_out, A[3]);
  and and_4 (and_4_out, not_4_out, B[3]);
  or or_1 (Salida, and_1_out, and_2_out, and_3_out, and_4_out);
endmodule

module Comparador (
  input  [3:0] A,
  input  [3:0] B,
  output [6:0] Salida_a_Dec
);

  wire [2:0] igualador_1_igualdad;

  Igualador igualador_1 (.A(A), .B(B), .Igualdad(igualador_1_igualdad[0]));
  Mayor mayor_1 (.A(A), .B(B), .Salida(igualador_1_igualdad[1]));
  Menor menor_1 (.A(A), .B(B), .Salida(igualador_1_igualdad[2]));
  Decoder_Comparador decoder_comparador_1 (
    .Entrada(igualador_1_igualdad), .a(Salida_a_Dec[6]), .c(Salida_a_Dec[4]), .d(Salida_a_Dec[3]),
    .e(Salida_a_Dec[2]), .f(Salida_a_Dec[1]), .g(Salida_a_Dec[0]), .b(Salida_a_Dec[5]));
endmodule

module Decoder_Comparador (
  input  [2:0] Entrada,
  output a,
  output b,
  output c,
  output d,
  output e,
  output f,
  output g
);

  wire and_1_out, and_3_out, not_1_out, not_2_out, not_3_out, not_4_out, not_5_out, not_6_out;

  not not_1 (not_1_out, Entrada[2]);
  not not_2 (not_2_out, Entrada[1]);
  not not_3 (not_3_out, Entrada[2]);
  not not_4 (not_4_out, Entrada[0]);
  not not_5 (not_5_out, Entrada[1]);
  not not_6 (not_6_out, Entrada[0]);
  and and_1 (and_1_out, not_1_out, not_2_out, Entrada[0]);
  and and_2 (c, not_3_out, Entrada[1], not_4_out);
  and and_3 (and_3_out, Entrada[2], not_5_out, not_6_out);
  or or_1 (a, and_1_out, c);
  or or_2 (d, and_1_out, c, and_3_out);

  assign b = 1'b0;
  assign e = d;
  assign f = d;
  assign g = a;
endmodule

module Dec_7_seg (
  input  [3:0] in_1,
  output a,
  output b,
  output c,
  output d,
  output e,
  output f,
  output g
);

  wire and_1_out, and_2_out, and_3_out, and_4_out, and_5_out, and_6_out, and_7_out, and_8_out, and_9_out,
       and_10_out, and_11_out, and_12_out, and_13_out, and_14_out, and_15_out, and_16_out, and_17_out,
       and_18_out, and_19_out, and_20_out, and_21_out, and_22_out, and_23_out, and_24_out, and_25_out,
       and_26_out, and_27_out, and_28_out, not_1_out, not_2_out, not_3_out, not_4_out, not_5_out, not_6_out,
       not_7_out, not_8_out, not_9_out, not_10_out, not_11_out, not_12_out, not_13_out, not_14_out,
       not_15_out, not_16_out, not_17_out, not_18_out, not_19_out, not_20_out, not_21_out, not_22_out,
       not_23_out, not_24_out, not_25_out, not_26_out, not_27_out, not_28_out, not_29_out, not_30_out,
       not_31_out, not_32_out, not_33_out, not_34_out, not_35_out, not_36_out, not_37_out, not_38_out,
       not_39_out, not_40_out, not_41_out, not_42_out, not_43_out, not_44_out, not_45_out, not_46_out,
       not_47_out, not_48_out, not_49_out, not_50_out, not_51_out, not_52_out, not_53_out, not_54_out,
       not_55_out, not_56_out, not_57_out;

  not not_1 (not_1_out, in_1[3]);
  not not_2 (not_2_out, in_1[2]);
  not not_3 (not_3_out, in_1[1]);
  not not_4 (not_4_out, in_1[3]);
  not not_5 (not_5_out, in_1[3]);
  not not_6 (not_6_out, in_1[2]);
  not not_7 (not_7_out, in_1[2]);
  not not_8 (not_8_out, in_1[1]);
  not not_9 (not_9_out, in_1[3]);
  not not_10 (not_10_out, in_1[1]);
  not not_11 (not_11_out, in_1[0]);
  not not_12 (not_12_out, in_1[3]);
  not not_13 (not_13_out, in_1[3]);
  not not_14 (not_14_out, in_1[1]);
  not not_15 (not_15_out, in_1[2]);
  not not_16 (not_16_out, in_1[1]);
  not not_17 (not_17_out, in_1[3]);
  not not_18 (not_18_out, in_1[3]);
  not not_19 (not_19_out, in_1[3]);
  not not_20 (not_20_out, in_1[2]);
  not not_21 (not_21_out, in_1[2]);
  not not_22 (not_22_out, in_1[1]);
  not not_23 (not_23_out, in_1[3]);
  not not_24 (not_24_out, in_1[2]);
  not not_25 (not_25_out, in_1[0]);
  not not_26 (not_26_out, in_1[3]);
  not not_27 (not_27_out, in_1[0]);
  not not_28 (not_28_out, in_1[3]);
  not not_29 (not_29_out, in_1[1]);
  not not_30 (not_30_out, in_1[3]);
  not not_31 (not_31_out, in_1[0]);
  not not_32 (not_32_out, in_1[3]);
  not not_33 (not_33_out, in_1[2]);
  not not_34 (not_34_out, in_1[0]);
  not not_35 (not_35_out, in_1[0]);
  not not_36 (not_36_out, in_1[2]);
  not not_37 (not_37_out, in_1[1]);
  not not_38 (not_38_out, in_1[3]);
  not not_39 (not_39_out, in_1[1]);
  not not_40 (not_40_out, in_1[2]);
  not not_41 (not_41_out, in_1[1]);
  not not_42 (not_42_out, in_1[3]);
  not not_43 (not_43_out, in_1[0]);
  not not_44 (not_44_out, in_1[3]);
  not not_45 (not_45_out, in_1[1]);
  not not_46 (not_46_out, in_1[0]);
  not not_47 (not_47_out, in_1[2]);
  not not_48 (not_48_out, in_1[1]);
  not not_49 (not_49_out, in_1[3]);
  not not_50 (not_50_out, in_1[1]);
  not not_51 (not_51_out, in_1[3]);
  not not_52 (not_52_out, in_1[2]);
  not not_53 (not_53_out, in_1[3]);
  not not_54 (not_54_out, in_1[0]);
  and and_1 (and_1_out, not_1_out, in_1[1]);
  and and_2 (and_2_out, in_1[3], not_2_out, not_3_out);
  and and_3 (and_3_out, not_4_out, in_1[2], in_1[0]);
  and and_4 (and_4_out, not_5_out, not_6_out);
  and and_5 (and_5_out, not_7_out, not_8_out);
  and and_6 (and_6_out, not_9_out, not_10_out, not_11_out);
  and and_7 (and_7_out, not_12_out, in_1[1], in_1[0]);
  and and_8 (and_8_out, not_13_out, not_14_out);
  and and_9 (and_9_out, not_15_out, not_16_out);
  and and_10 (and_10_out, not_17_out, in_1[0]);
  and and_11 (and_11_out, not_18_out, in_1[2], in_1[1]);
  and and_12 (and_12_out, not_19_out, not_20_out, in_1[1]);
  and and_13 (and_13_out, in_1[3], not_21_out, not_22_out);
  and and_14 (and_14_out, not_23_out, not_24_out, not_25_out);
  and and_15 (and_15_out, not_26_out, in_1[1], not_27_out);
  and and_16 (and_16_out, not_28_out, in_1[2], not_29_out, in_1[0]);
  and and_17 (and_17_out, not_30_out, in_1[1], not_31_out);
  and and_18 (and_18_out, not_32_out, not_33_out, not_34_out);
  and and_19 (and_19_out, not_35_out, not_36_out, not_37_out);
  and and_20 (and_20_out, not_38_out, in_1[2], not_39_out);
  and and_21 (and_21_out, in_1[3], not_40_out, not_41_out);
  and and_22 (and_22_out, not_42_out, in_1[2], not_43_out);
  and and_23 (and_23_out, not_44_out, not_45_out, not_46_out);
  and and_24 (and_24_out, in_1[3], not_47_out, not_48_out);
  and and_25 (and_25_out, not_49_out, in_1[2], not_50_out);
  and and_26 (and_26_out, not_51_out, not_52_out, in_1[1]);
  and and_27 (and_27_out, not_53_out, in_1[1], not_54_out);
  not not_55 (not_55_out, in_1[2]);
  not not_56 (not_56_out, in_1[1]);
  not not_57 (not_57_out, in_1[0]);
  and and_28 (and_28_out, not_55_out, not_56_out, not_57_out);
  or or_1 (a, and_1_out, and_2_out, and_28_out, and_3_out);
  or or_2 (b, and_4_out, and_5_out, and_6_out, and_7_out);
  or or_3 (c, and_8_out, and_9_out, and_10_out, and_11_out);
  or or_4 (d, and_12_out, and_13_out, and_14_out, and_15_out, and_16_out);
  or or_5 (e, and_17_out, and_18_out, and_19_out);
  or or_6 (f, and_20_out, and_21_out, and_22_out, and_23_out);
  or or_7 (g, and_24_out, and_25_out, and_26_out, and_27_out);
endmodule

module Complemento_a_2 (
  input  [3:0] Entrada,
  output [3:0] Salida
);

  wire and_1_out, and_2_out, and_3_out, and_4_out, and_5_out, and_6_out, and_7_out, and_8_out, and_9_out,
       and_10_out, and_11_out, and_12_out, and_13_out, not_1_out, not_2_out, not_3_out, not_4_out, not_5_out,
       not_6_out, not_7_out, not_8_out, not_9_out, not_10_out, not_11_out, not_12_out, not_13_out,
       not_14_out, not_15_out, not_16_out, not_17_out, not_18_out, not_19_out, not_20_out;

  not not_1 (not_1_out, Entrada[3]);
  not not_2 (not_2_out, Entrada[3]);
  not not_3 (not_3_out, Entrada[3]);
  not not_4 (not_4_out, Entrada[2]);
  not not_5 (not_5_out, Entrada[1]);
  not not_6 (not_6_out, Entrada[3]);
  not not_7 (not_7_out, Entrada[2]);
  not not_8 (not_8_out, Entrada[3]);
  not not_9 (not_9_out, Entrada[2]);
  not not_10 (not_10_out, Entrada[2]);
  not not_11 (not_11_out, Entrada[1]);
  not not_12 (not_12_out, Entrada[3]);
  not not_13 (not_13_out, Entrada[1]);
  not not_14 (not_14_out, Entrada[0]);
  not not_15 (not_15_out, Entrada[3]);
  not not_16 (not_16_out, Entrada[1]);
  not not_17 (not_17_out, Entrada[2]);
  not not_18 (not_18_out, Entrada[1]);
  not not_19 (not_19_out, Entrada[3]);
  and and_1 (and_1_out, not_1_out, Entrada[2]);
  and and_2 (and_2_out, not_2_out, Entrada[0]);
  and and_3 (and_3_out, not_3_out, Entrada[1]);
  and and_4 (and_4_out, Entrada[3], not_4_out, not_5_out);
  and and_5 (and_5_out, not_6_out, not_7_out, Entrada[0]);
  and and_6 (and_6_out, not_8_out, not_9_out, Entrada[1]);
  and and_7 (and_7_out, Entrada[3], not_10_out, not_11_out, Entrada[0]);
  and and_8 (and_8_out, not_12_out, Entrada[2], not_13_out, not_14_out);
  not not_20 (not_20_out, Entrada[0]);
  and and_9 (and_9_out, not_19_out, Entrada[0]);
  and and_10 (and_10_out, not_17_out, not_18_out, Entrada[0]);
  and and_11 (and_11_out, not_15_out, not_16_out, Entrada[0]);
  and and_12 (and_12_out, not_15_out, Entrada[1], not_20_out);
  and and_13 (and_13_out, not_17_out, not_18_out, Entrada[0]);
  or or_1 (Salida[3], and_1_out, and_2_out, and_3_out, and_4_out);
  or or_2 (Salida[2], and_5_out, and_6_out, and_7_out, and_8_out);
  or or_3 (Salida[1], and_11_out, and_12_out, and_13_out);
  or or_4 (Salida[0], and_9_out, and_10_out);
endmodule

module Sumador_5_bits (
  input  [4:0] A,
  input  [4:0] B,
  output [4:0] S,
  output C1
);

  wire and_1_out, and_2_out, and_3_out, and_4_out, and_5_out, and_6_out, and_7_out, and_8_out, and_9_out,
       or_1_out, or_2_out, or_3_out, xor_2_out, xor_3_out, xor_4_out, xor_5_out, xor_6_out, xor_7_out,
       xor_8_out, xor_9_out;

  xor xor_1 (S[0], A[0], B[0]);
  and and_1 (and_1_out, A[0], B[0]);
  xor xor_2 (xor_2_out, A[1], B[1]);
  xor xor_3 (xor_3_out, A[2], B[2]);
  and and_2 (and_2_out, A[1], B[1]);
  and and_3 (and_3_out, and_1_out, xor_2_out);
  xor xor_4 (xor_4_out, A[3], B[3]);
  xor xor_5 (xor_5_out, A[4], B[4]);
  xor xor_6 (xor_6_out, A[1], B[1]);
  xor xor_7 (xor_7_out, A[2], B[2]);
  and and_4 (and_4_out, A[2], B[2]);
  and and_5 (and_5_out, or_1_out, xor_3_out);
  xor xor_8 (xor_8_out, A[3], B[3]);
  and and_6 (and_6_out, A[3], B[3]);
  and and_7 (and_7_out, or_2_out, xor_4_out);
  xor xor_9 (xor_9_out, A[4], B[4]);
  and and_8 (and_8_out, A[4], B[4]);
  and and_9 (and_9_out, or_3_out, xor_5_out);
  xor xor_10 (S[1], xor_6_out, and_1_out);
  or or_1 (or_1_out, and_2_out, and_3_out);
  xor xor_11 (S[2], xor_7_out, or_1_out);
  or or_2 (or_2_out, and_4_out, and_5_out);
  xor xor_12 (S[3], xor_8_out, or_2_out);
  or or_3 (or_3_out, and_6_out, and_7_out);
  xor xor_13 (S[4], xor_9_out, or_3_out);
  or or_4 (C1, and_8_out, and_9_out);
endmodule

module Sumador_6_bits (
  input  [5:0] A,
  input  [5:0] B,
  output [5:0] S,
  output C1
);

  wire and_1_out, and_2_out, and_3_out, and_4_out, and_5_out, and_6_out, and_7_out, and_8_out, and_9_out,
       and_10_out, and_11_out, or_1_out, or_2_out, or_3_out, or_4_out, xor_2_out, xor_3_out, xor_4_out,
       xor_5_out, xor_6_out, xor_7_out, xor_8_out, xor_9_out, xor_10_out, xor_11_out;

  xor xor_1 (S[0], A[0], B[0]);
  and and_1 (and_1_out, A[0], B[0]);
  xor xor_2 (xor_2_out, A[1], B[1]);
  xor xor_3 (xor_3_out, A[2], B[2]);
  and and_2 (and_2_out, A[1], B[1]);
  and and_3 (and_3_out, and_1_out, xor_2_out);
  xor xor_4 (xor_4_out, A[3], B[3]);
  xor xor_5 (xor_5_out, A[4], B[4]);
  xor xor_6 (xor_6_out, A[5], B[5]);
  xor xor_7 (xor_7_out, A[1], B[1]);
  xor xor_8 (xor_8_out, A[2], B[2]);
  and and_4 (and_4_out, A[2], B[2]);
  and and_5 (and_5_out, or_1_out, xor_3_out);
  xor xor_9 (xor_9_out, A[3], B[3]);
  and and_6 (and_6_out, A[3], B[3]);
  and and_7 (and_7_out, or_2_out, xor_4_out);
  xor xor_10 (xor_10_out, A[4], B[4]);
  and and_8 (and_8_out, A[4], B[4]);
  and and_9 (and_9_out, or_3_out, xor_5_out);
  xor xor_11 (xor_11_out, A[5], B[5]);
  and and_10 (and_10_out, A[5], B[5]);
  and and_11 (and_11_out, or_4_out, xor_6_out);
  xor xor_12 (S[1], xor_7_out, and_1_out);
  or or_1 (or_1_out, and_2_out, and_3_out);
  xor xor_13 (S[2], xor_8_out, or_1_out);
  or or_2 (or_2_out, and_4_out, and_5_out);
  xor xor_14 (S[3], xor_9_out, or_2_out);
  or or_3 (or_3_out, and_6_out, and_7_out);
  xor xor_15 (S[4], xor_10_out, or_3_out);
  or or_4 (or_4_out, and_8_out, and_9_out);
  xor xor_16 (S[5], xor_11_out, or_4_out);
  or or_5 (C1, and_10_out, and_11_out);
endmodule
